# Fritzing sketch AirQuality (saved by Fritzing 0.9.6b)
circuit board: 15.4cm x 7.88647cm
breadboards: 1

parts:
  microSD = MicroSD Card Module
  OLED_124x64 = Grove OLED 128x96
  R1 = Resistor [tolerance=±5% power=0.25 resistance=10k package=THT]
  DHT22 = DHT22 Humidity and Temperature Sensor
  MQ_135 = MQ-7 breakout
  RTC = ZS-042 RTC Module
  U2 = ESP32-38PinWide [part_number=ESP32-38PinWide]

nets:
  GND: microSD.GND, OLED_124x64.GND, DHT22.GND, MQ_135.GND, RTC.GND, U2.GND
  VCC: microSD.VCC, OLED_124x64.VCC, R1.Pin_1, DHT22.VDD, MQ_135.VCC, RTC.VCC, U2.VIN
  N1: microSD.MISO, U2.GPIO19
  N2: microSD.MOSI, U2.GPIO23
  N3: microSD.SCK, U2.GPIO18
  N4: microSD.CS, U2.GPIO5
  N5: OLED_124x64.SDA, RTC.SDA, U2.GPIO21
  N6: OLED_124x64.SCL, RTC.SCL, U2.GPIO22
  N7: R1.Pin_0, DHT22.DATA, U2.GPIO35
  N8: MQ_135.AO, U2.GPIO25

custom parts:
  MQ-7 breakout: SKU: 101282
  ESP32-38PinWide: Generic 38-Pin ESP32 with wide format (only access to one side of pins on a breadboard) based on Stephen Lilley's HiLetgo ESP-WROOM-32 ESP32 ESP-32S Development Board.
